# Fritzing sketch hardware (saved by Fritzing 0.9.3b)
circuit board: 2.42062cm x 3.29516cm
breadboards: 1

parts:
  J1 = male pin header, 1 pin [form="♂ (male)"]
  J2 = male pin header, 1 pin [form="♂ (male)"]
  R1 = Resistor [tolerance=±5% resistance=10k package=THT]
  J3 = male pin header, 1 pin [form="♂ (male)"]
  J4 = male pin header, 1 pin [form="♂ (male)"]
  J5 = male pin header, 1 pin [form="♂ (male)"]
  R2 = Resistor [tolerance=±5% resistance=470 package=THT]
  R3 = Resistor [tolerance=±5% resistance=470 package=THT]
  R4 = Resistor [tolerance=±5% resistance=470 package=THT]
  R5 = Resistor [tolerance=±5% resistance=470 package=THT]
  R6 = Resistor [tolerance=±5% resistance=470 package=THT]
  R7 = Resistor [tolerance=±5% resistance=470 package=THT]
  R8 = Resistor [tolerance=±5% resistance=470 package=THT]
  R9 = Resistor [tolerance=±5% resistance=470 package=THT]
  R10 = Resistor [tolerance=±5% resistance=470 package=THT]
  R11 = Resistor [tolerance=±5% resistance=470 package=THT]
  J8 = male pin header, 10 pins [form="♂ (male)"]
  J7 = male pin header, 10 pins [form="♂ (male)"]
  J6 = male pin header, 5 pins [form="♂ (male)"]
  J9 = male pin header, 5 pins [form="♂ (male)"]

nets:
  N1: J1.pin1, J4.pin1, R2.Pin_1, R3.Pin_1, R4.Pin_1, R5.Pin_1, R6.Pin_1, R7.Pin_1, R8.Pin_1, R9.Pin_1, R10.Pin_1, R11.Pin_1
  N2: J2.pin1, R1.Pin_0
  N3: R1.Pin_1, J3.pin1, J5.pin1
  N4: R2.Pin_0, J6.pin1
  N5: R3.Pin_0, J6.pin2
  N6: R4.Pin_0, J6.pin3
  N7: R5.Pin_0, J6.pin4
  N8: R6.Pin_0, J6.pin5
  N9: R7.Pin_0, J9.pin1
  N10: R8.Pin_0, J9.pin2
  N11: R9.Pin_0, J9.pin3
  N12: R10.Pin_0, J9.pin4
  N13: R11.Pin_0, J9.pin5
  N14: J8.pin1, J7.pin1
  N15: J8.pin2, J7.pin2
  N16: J8.pin3, J7.pin3
  N17: J8.pin4, J7.pin4
  N18: J8.pin5, J7.pin5
  N19: J8.pin6, J7.pin6
  N20: J8.pin7, J7.pin7
  N21: J8.pin8, J7.pin8
  N22: J8.pin9, J7.pin9
  N23: J8.pin10, J7.pin10
